// Logisim project alu.circ as structural Verilog: 1 circuit, main circuit main
module main (
  input  [31:0] X,
  input  [31:0] Y,
  input  [3:0] Switch,
  output Equal,
  output [31:0] Result
);

  wire comparator_2_lt;
  wire [4:0] bit_extender_1_out, bit_extender_2_out;
  wire [31:0] add, \and , div, mulh, mult, \or , rem, sll, slt, srl, sub, \xor ;

  Comparator #(.width(32)) comparator_1 (.a(X), .b(Y), .eq(Equal));  // open: gt, lt
  Bit_Extender #(.in_width(32), .out_width(5)) bit_extender_1 (.in(Y), .out(bit_extender_1_out));
  assign \and  = X & Y;  // AND_Gate and_1, 32 bits wide
  assign \or  = X | Y;  // OR_Gate or_1, 32 bits wide
  assign \xor  = X ^ Y;  // XOR_Gate xor_1, 32 bits wide
  Comparator #(.width(32)) comparator_2 (.a(X), .b(Y), .lt(comparator_2_lt));  // open: gt, eq
  Multiplier #(.width(32)) multiplier_1 (.a(X), .b(Y), .out(mult));  // open: cin, cout
  Multiplier #(.width(32)) multiplier_2 (.a(X), .b(Y), .cout(mulh));  // open: out, cin
  Divider #(.width(32)) divider_1 (.a(X), .b(Y), .out(div));  // open: upper, rem
  Divider #(.width(32)) divider_2 (.a(X), .b(Y), .rem(rem));  // open: out, upper
  Bit_Extender #(.in_width(32), .out_width(5)) bit_extender_2 (.in(Y), .out(bit_extender_2_out));
  Adder #(.width(32)) adder_1 (.a(X), .b(Y), .out(add));  // open: cin, cout
  Subtractor #(.width(32)) subtractor_1 (.a(X), .b(Y), .out(sub));  // open: bin, bout
  Shifter #(.width(32)) shifter_1 (.in(X), .\dist (bit_extender_2_out), .out(sll));
  assign slt = {{31{1'b0}}, comparator_2_lt};  // Bit_Extender bit_extender_3
  Shifter #(.width(32), .shift("lr")) shifter_2 (.in(X), .\dist (bit_extender_1_out), .out(srl));
  Multiplexer #(.select(4), .width(32), .enable("false")) multiplexer_1 (
    .in0(sll), .in1(srl), .in2(add), .in3(\and ), .in4(\or ), .in5(\xor ), .in6(slt), .in7(mult), .in8(mulh),
    .in9(div), .in10(rem), .in11(sub), .in12(Y), .out(Result), .sel(Switch));  // open: in13, in14, in15

  // Other names for the same wires on the sheet: lui[31:0] = Y; S[3:0] = Switch

  // Notes on the sheet:
  //   INPUTS to your circuit
  //   DON'T CHANGE THE LOCATIONS OF THE INPUTS AND OUTPUTS!
  //   OUTPUTS from your circuit
endmodule
