// Logisim project regfile.circ as structural Verilog: 1 circuit, main circuit main
module main (
  input  [4:0] Read_Register_1__rs1,
  input  [4:0] Read_Register_2__rs2,
  input  [4:0] Write_Register__rd,
  input  [31:0] Write_Data,
  input  Write_Enable,
  input  Clock,
  output [31:0] s0_Value,
  output [31:0] s1_Value,
  output [31:0] t0_Value,
  output [31:0] t1_Value,
  output [31:0] a0_Value,
  output [31:0] ra_Value,
  output [31:0] sp_Value,
  output [31:0] Read_Data_1,
  output [31:0] Read_Data_2
);

  wire a0en, a1en, demultiplexer_1_out28, multiplexer_1_p1, multiplexer_1_p11, raen, s0en, s1en, spen, t0en,
       t1en, zeroen;
  wire [31:0] a1out, zeroout;

  Register #(.width(32)) zero (.Q(zeroout), .clk(Clock));  // open: D, en, clr
  Register #(.width(32)) ra (.D(Write_Data), .en(raen), .Q(ra_Value), .clk(Clock));  // open: clr
  Demultiplexer #(.select(5), .disabled(0), .enable("false")) demultiplexer_1 (
    .out0(zeroen), .out1(raen), .out2(spen), .out5(t0en), .out6(t1en), .out8(s0en), .out9(s1en),
    .out10(a0en), .out11(a1en), .out28(demultiplexer_1_out28), .out29(demultiplexer_1_out28),
    .in(Write_Enable), .sel(Write_Register__rd));  // open: out3, out4, out7, out12, out13, out14, out15, out16, out17, out18, out19, out20, out21, out22, out23, out24, out25, out26, out27, out30, out31
  Register #(.width(32)) sp (.D(Write_Data), .en(spen), .Q(sp_Value), .clk(Clock));  // open: clr
  Register #(.width(32)) t0 (.D(Write_Data), .en(t0en), .Q(t0_Value), .clk(Clock));  // open: clr
  Register #(.width(32)) t1 (.D(Write_Data), .en(t1en), .Q(t1_Value), .clk(Clock));  // open: clr
  // Multiplexer #(.select(5), .width(32), .enable("false")) multiplexer_1: pin names not known; wires that end beside it: multiplexer_1_p1, zeroout, ra_Value, sp_Value, t0_Value, t1_Value, s0_Value, s1_Value, a0_Value, a1out, multiplexer_1_p11, Read_Register_1__rs1, Read_Data_1
  Register #(.width(32)) s0 (.D(Write_Data), .en(s0en), .Q(s0_Value), .clk(Clock));  // open: clr
  Register #(.width(32)) s1 (.D(Write_Data), .en(s1en), .Q(s1_Value), .clk(Clock));  // open: clr
  Multiplexer #(.select(5), .width(32), .enable("false")) multiplexer_2 (
    .in0(zeroout), .in1(ra_Value), .in2(sp_Value), .in5(t0_Value), .in6(t1_Value), .in8(s0_Value),
    .in9(s1_Value), .in10(a0_Value), .in11(a1out), .out(Read_Data_2), .sel(Read_Register_2__rs2));  // open: in3, in4, in7, in12, in13, in14, in15, in16, in17, in18, in19, in20, in21, in22, in23, in24, in25, in26, in27, in28, in29, in30, in31
  Register #(.width(32)) a0 (.D(Write_Data), .en(a0en), .Q(a0_Value), .clk(Clock));  // open: clr
  Register #(.width(32)) a1 (.D(Write_Data), .en(a1en), .Q(a1out), .clk(Clock));  // open: clr

  // Other names for the same wires on the sheet: a0out[31:0] = a0_Value; clk = Clock; raout[31:0] = ra_Value;
  //   read_data1[31:0] = Read_Data_1; read_data2[31:0] = Read_Data_2; read_reg1[4:0] = Read_Register_1__rs1;
  //   read_reg2[4:0] = Read_Register_2__rs2; s0out[31:0] = s0_Value; s1out[31:0] = s1_Value; spout[31:0] = sp_Value;
  //   t0out[31:0] = t0_Value; t1out[31:0] = t1_Value; write_en = Write_Enable; write_reg[4:0] = Write_Register__rd

  // Notes on the sheet:
  //   INPUTS to your circuit
  //   These are DEBUG/TEST outputs from your circuit.
  //   OUTPUTS from your circuit
endmodule
