// Logisim project cpu.circ as structural Verilog: 5 circuits, main circuit main
module main (
  input  [31:0] INSTRUCTION,
  input  CLOCK,
  output [31:0] FETCH_ADDRESS,
  output [31:0] s0_Value,
  output [31:0] s1_Value,
  output [31:0] t0_Value,
  output [31:0] t1_Value,
  output [31:0] a0_Value,
  output [31:0] ra_Value,
  output [31:0] sp_Value
);

  wire ASel, BrEq, BrLT, BrLTU, BSel, MEM_p1, MEM_p4, MEM_p9, MEM_p13, MEM_p15, MemWEn, nop, PCSel, RegWEn;
  wire [2:0] funct3, WBSel;
  wire [3:0] ALUSel;
  wire [6:0] funct7;
  wire [7:0] multiplexer_5_out;
  wire [15:0] multiplexer_6_out;
  wire [24:0] INSTRUCTIONEx;
  wire [31:0] adder_1_out, adder_2_out, ALURes, immgen_1_immediate, LB, LHW, LoadedData, multiplexer_1_out,
       multiplexer_2_out, multiplexer_3_out, multiplexer_4_out, PC_q, PCx, r1dat, r2dat, shifter_2_out,
       WBData;

  // Probe on multiplexer_1_out
  Multiplexer #(.width(32), .enable("false")) multiplexer_1 (
    .in0(adder_1_out), .in1(ALURes), .out(multiplexer_1_out), .sel(PCSel));
  // Probe on PC_q
  // Probe on {funct7, INSTRUCTIONEx[24:15], funct3, INSTRUCTIONEx[11:0]}
  Register #(.width(32)) PC (.D(multiplexer_1_out), .Q(PC_q), .clk(CLOCK));  // open: en, clr
  Control_Module Control_Module (
    .opcode(INSTRUCTIONEx[6:0]), .func3(funct3), .BrLT(BrLT), .BrEq(BrEq), .BrLTU(BrLTU), .WBSel(WBSel),
    .MemWEn(MemWEn), .BSel(BSel), .RegWEn(RegWEn), .PCSel(PCSel), .ASel(ASel));
  Multiplexer #(.width(32), .enable("false")) multiplexer_2 (
    .in0(INSTRUCTION), .in1({32{1'b0}}), .out(multiplexer_2_out), .sel(nop));
  Comparator #(.width(1)) comparator_1 (.a(PCSel), .b(1'b1), .eq(nop));  // open: gt, lt
  Adder #(.width(32)) adder_1 (.a(32'h4), .b(PC_q), .out(adder_1_out));  // open: cin, cout
  Register #(.width(32)) u_PCx (.D(PC_q), .Q(PCx), .clk(CLOCK));  // open: en, clr
  Shifter #(.width(32), .shift("lr")) shifter_1 (.in(PC_q), .\dist (5'b00010), .out(FETCH_ADDRESS));
  Register #(.width(32)) InstrX (
    .D(multiplexer_2_out), .Q({funct7, INSTRUCTIONEx[24:15], funct3, INSTRUCTIONEx[11:0]}), .clk(CLOCK));  // open: en, clr
  // Probe on INSTRUCTIONEx[19:15]
  // Probe on INSTRUCTIONEx[24:20]
  // Probe on INSTRUCTIONEx[11:7]
  Branch_Comparator branch_comparator_1 (
    .Instruction({funct7, INSTRUCTIONEx[24:15], funct3, INSTRUCTIONEx[11:0]}), .r2dat(r2dat), .r1dat(r1dat),
    .BrLT(BrLT), .BrEq(BrEq), .BrLTU(BrLTU));
  regfile_main main_1 (
    .Read_Register_1__rs1(INSTRUCTIONEx[19:15]), .Read_Register_2__rs2(INSTRUCTIONEx[24:20]),
    .Write_Register__rd(INSTRUCTIONEx[11:7]), .Write_Data(WBData), .Write_Enable(RegWEn), .Clock(CLOCK),
    .Read_Data_1(r1dat), .Read_Data_2(r2dat), .s1_Value(s1_Value), .t0_Value(t0_Value), .t1_Value(t1_Value),
    .a0_Value(a0_Value), .s0_Value(s0_Value), .ra_Value(ra_Value), .sp_Value(sp_Value));
  ImmGen immgen_1 (
    .funct7(funct7), .Instruction({funct7, INSTRUCTIONEx[24:15], funct3, INSTRUCTIONEx[11:0]}),
    .Opcode(INSTRUCTIONEx[6:0]), .funct3(funct3), .Immediate(immgen_1_immediate));
  ALUSel alusel_1 (
    .PCSel(PCSel), .MemWEn(MemWEn), .OpCode(INSTRUCTIONEx[6:0]), .func3(funct3), .func7(funct7),
    .ALUSel(ALUSel));
  // Probe on immgen_1_immediate
  Multiplexer #(.width(32), .disabled(0), .enable("false")) multiplexer_3 (
    .in0(PCx), .in1(r1dat), .out(multiplexer_3_out), .sel(ASel));
  Multiplexer #(.width(32), .disabled(0), .enable("false")) multiplexer_4 (
    .in0(r2dat), .in1(immgen_1_immediate), .out(multiplexer_4_out), .sel(BSel));
  alu_main main_2 (.Switch(ALUSel), .X(multiplexer_3_out), .Result(ALURes), .Y(multiplexer_4_out));  // open: Equal
  // Probe on ALUSel
  Shifter #(.width(32), .shift("lr")) shifter_2 (.in(ALURes), .\dist (5'b00010), .out(shifter_2_out));
  // mem_main MEM: pin names not known; wires that end beside it: MEM_p1, MEM_p1, ALURes[1:0], MEM_p4, MEM_p4, shifter_2_out, r2dat, MemWEn, MEM_p9, CLOCK, MEM_p9, LoadedData, MEM_p13, MEM_p13, MEM_p15
  Multiplexer #(.select(2), .width(8), .enable("false")) multiplexer_5 (
    .in0(LoadedData[7:0]), .in1(LoadedData[15:8]), .in2(LoadedData[23:16]), .in3(LoadedData[31:24]),
    .out(multiplexer_5_out), .sel(ALURes[1:0]));
  Multiplexer #(.width(16), .enable("false")) multiplexer_6 (
    .in0(LoadedData[15:0]), .out(multiplexer_6_out), .sel(ALURes[1]));  // open: in1
  Adder #(.width(32)) adder_2 (.a(32'h4), .b(PCx), .out(adder_2_out));  // open: cin, cout
  assign LHW = {{16{multiplexer_6_out[15]}}, multiplexer_6_out};  // Bit_Extender bit_extender_1
  assign LB = {{24{multiplexer_5_out[7]}}, multiplexer_5_out};  // Bit_Extender bit_extender_2
  Multiplexer #(.select(3), .width(32), .enable("false")) multiplexer_7 (
    .in0(adder_2_out), .in1(ALURes), .in2(LoadedData), .in3(LHW), .in4(LB), .out(WBData), .sel(WBSel));  // open: in5, in6, in7
  // Probe on WBSel

  // Other names for the same wires on the sheet: a0out[31:0] = a0_Value; ByteSel[1:0] = ALURes[1:0];
  //   LoadOffset[1:0] = ALURes[1:0]; HWsel = ALURes[1]; clk = CLOCK; fetch_addr[31:0] = FETCH_ADDRESS;
  //   opcode[6:0] = INSTRUCTIONEx[6:0]; rd[4:0] = INSTRUCTIONEx[11:7]; INSTRUCTIONEx (some bits) = {funct7, funct3};
  //   rs1[4:0] = INSTRUCTIONEx[19:15]; rs2[4:0] = INSTRUCTIONEx[24:20]; raout[31:0] = ra_Value;
  //   s0out[31:0] = s0_Value; s1out[31:0] = s1_Value; spout[31:0] = sp_Value; t0out[31:0] = t0_Value;
  //   t1out[31:0] = t1_Value

  // Notes on the sheet:
  //   Output
  //   Pipeline
  //   These are outputs/inputs from run.circ
  //   Inputs
  //   Branch Comparator
  //   These are DEBUG/TEST outputs from your circuit.
endmodule

module Control_Module (
  input  [6:0] opcode,
  input  [2:0] func3,
  input  BrLT,
  input  BrEq,
  input  BrLTU,
  output [2:0] WBSel,
  output MemWEn,
  output BSel,
  output RegWEn,
  output PCSel,
  output ASel
);

  wire and_1_out, and_2_out, and_3_out, and_4_out, comparator_1_eq, comparator_2_eq, comparator_3_eq,
       comparator_4_eq, comparator_5_eq, comparator_6_eq, comparator_7_eq, comparator_8_eq, comparator_9_eq,
       comparator_10_eq, comparator_11_eq, comparator_12_eq, comparator_13_eq, comparator_14_eq,
       comparator_15_eq, comparator_16_eq, comparator_17_eq, comparator_18_eq, comparator_19_eq,
       comparator_20_eq, comparator_22_eq, comparator_23_eq, comparator_24_eq, comparator_25_eq, or_2_out,
       or_3_out, or_4_out, or_6_out;
  wire [2:0] Step1, Step2, Step3, Step4;

  Comparator #(.width(7), .mode("unsigned")) comparator_1 (
    .a(7'b0110011), .b(opcode), .eq(comparator_1_eq));  // open: gt, lt
  Comparator #(.width(7), .mode("unsigned")) comparator_2 (
    .a(7'b0000011), .b(opcode), .eq(comparator_2_eq));  // open: gt, lt
  Comparator #(.width(7), .mode("unsigned")) comparator_3 (
    .a(7'b0010011), .b(opcode), .eq(comparator_3_eq));  // open: gt, lt
  Comparator #(.width(7), .mode("unsigned")) comparator_4 (
    .a(7'b0110111), .b(opcode), .eq(comparator_4_eq));  // open: gt, lt
  Comparator #(.width(7), .mode("unsigned")) comparator_5 (
    .a(7'b1101111), .b(opcode), .eq(comparator_5_eq));  // open: gt, lt
  Comparator #(.width(7), .mode("unsigned")) comparator_6 (
    .a(7'b1100111), .b(opcode), .eq(comparator_6_eq));  // open: gt, lt
  or or_1 (RegWEn, comparator_1_eq, comparator_2_eq, comparator_3_eq, comparator_4_eq, comparator_5_eq, comparator_6_eq);
  Comparator #(.width(7), .mode("unsigned")) comparator_7 (
    .a(7'b1101111), .b(opcode), .eq(comparator_7_eq));  // open: gt, lt
  Comparator #(.width(7), .mode("unsigned")) comparator_8 (
    .a(7'b1100111), .b(opcode), .eq(comparator_8_eq));  // open: gt, lt
  Comparator #(.width(7), .mode("unsigned")) comparator_9 (
    .a(7'b0110011), .b(opcode), .eq(comparator_9_eq));  // open: gt, lt
  Comparator #(.width(7), .mode("unsigned")) comparator_10 (
    .a(7'b0010011), .b(opcode), .eq(comparator_10_eq));  // open: gt, lt
  Comparator #(.width(7), .mode("unsigned")) comparator_11 (
    .a(7'b0110111), .b(opcode), .eq(comparator_11_eq));  // open: gt, lt
  Comparator #(.width(3)) comparator_12 (.a(3'b000), .b(func3), .eq(comparator_12_eq));  // open: gt, lt
  Comparator #(.width(7), .mode("unsigned")) comparator_13 (
    .a(7'b0000011), .b(opcode), .eq(comparator_13_eq));  // open: gt, lt
  Comparator #(.width(3)) comparator_14 (.a(3'b001), .b(func3), .eq(comparator_14_eq));  // open: gt, lt
  Comparator #(.width(7), .mode("unsigned")) comparator_15 (
    .a(7'b0000011), .b(opcode), .eq(comparator_15_eq));  // open: gt, lt
  Comparator #(.width(3)) comparator_16 (.a(3'b010), .b(func3), .eq(comparator_16_eq));  // open: gt, lt
  Comparator #(.width(7), .mode("unsigned")) comparator_17 (
    .a(7'b0000011), .b(opcode), .eq(comparator_17_eq));  // open: gt, lt
  or or_2 (or_2_out, comparator_7_eq, comparator_8_eq);
  and and_1 (and_1_out, comparator_12_eq, comparator_13_eq);
  and and_2 (and_2_out, comparator_14_eq, comparator_15_eq);
  and and_3 (and_3_out, comparator_16_eq, comparator_17_eq);
  Comparator #(.width(7), .mode("unsigned")) comparator_18 (
    .a(7'b1100011), .b(opcode), .eq(comparator_18_eq));  // open: gt, lt
  or or_3 (or_3_out, BrLT, BrEq, BrLTU);
  Comparator #(.width(7), .mode("unsigned")) comparator_19 (
    .a(7'b1101111), .b(opcode), .eq(comparator_19_eq));  // open: gt, lt
  Comparator #(.width(7), .mode("unsigned")) comparator_20 (
    .a(7'b1100111), .b(opcode), .eq(comparator_20_eq));  // open: gt, lt
  Multiplexer #(.width(3), .enable("false")) multiplexer_1 (.in0(3'b110), .in1(3'b000), .out(Step4), .sel(or_2_out));
  or or_4 (or_4_out, comparator_9_eq, comparator_10_eq, comparator_11_eq);
  Multiplexer #(.width(3), .disabled(0), .enable("false")) multiplexer_2 (
    .in0(Step3), .in1(3'b100), .out(Step2), .sel(and_1_out));
  Multiplexer #(.width(3), .disabled(0), .enable("false")) multiplexer_3 (
    .in0(Step2), .in1(3'b011), .out(Step1), .sel(and_2_out));
  Multiplexer #(.width(3), .enable("false")) multiplexer_4 (.in0(Step1), .in1(3'b010), .out(WBSel), .sel(and_3_out));
  and and_4 (and_4_out, comparator_18_eq, or_3_out);
  Multiplexer #(.width(3), .disabled(0), .enable("false")) multiplexer_5 (
    .in0(Step4), .in1(3'b001), .out(Step3), .sel(or_4_out));
  or or_5 (PCSel, and_4_out, comparator_19_eq, comparator_20_eq);
  Comparator #(.width(7), .mode("unsigned")) comparator_21 (.a(7'b0100011), .b(opcode), .eq(MemWEn));  // open: gt, lt
  Comparator #(.width(7), .mode("unsigned")) comparator_22 (
    .a(7'b0110011), .b(opcode), .eq(comparator_22_eq));  // open: gt, lt
  Comparator #(.width(7), .mode("unsigned")) comparator_23 (
    .a(7'b1100011), .b(opcode), .eq(comparator_23_eq));  // open: gt, lt
  Comparator #(.width(7), .mode("unsigned")) comparator_24 (
    .a(7'b1101111), .b(opcode), .eq(comparator_24_eq));  // open: gt, lt
  Comparator #(.width(7), .mode("unsigned")) comparator_25 (
    .a(7'b0110111), .b(opcode), .eq(comparator_25_eq));  // open: gt, lt
  not not_1 (BSel, comparator_22_eq);
  or or_6 (or_6_out, comparator_23_eq, comparator_24_eq, comparator_25_eq);
  not not_2 (ASel, or_6_out);

  // Other names for the same wires on the sheet: WBSelVal[2:0] = WBSel
endmodule

// IG
module ImmGen (
  input  [6:0] funct7,
  input  [2:0] funct3,
  input  [6:0] Opcode,
  input  [31:0] Instruction,
  output [31:0] Immediate
);

  wire and_1_out, and_2_out, comparator_1_eq, comparator_2_eq, comparator_3_eq, comparator_4_eq, or_1_out;
  wire [31:0] adder_1_out, adder_2_out, adder_3_out, adder_4_out, bit_extender_1_out, bit_extender_2_out,
       bit_extender_3_out, bit_extender_4_out, bit_extender_5_out, bit_extender_6_out, bit_extender_7_out,
       bit_extender_8_out, bit_extender_9_out, bit_extender_11_out, bit_extender_12_out, bit_extender_13_out,
       Imm, ImmI, ImmS, ImmSB, ImmU, ImmUJ, shifter_1_out, shifter_2_out, shifter_3_out, shifter_4_out,
       shifter_5_out, shifter_6_out, shifter_7_out, shifter_8_out, shifter_10_out;

  assign bit_extender_1_out = {{24{1'b0}}, Instruction[19:12]};  // Bit_Extender bit_extender_1
  Shifter #(.width(32)) shifter_1 (.in(bit_extender_1_out), .\dist (5'b01100), .out(shifter_1_out));
  assign bit_extender_2_out = {{31{1'b0}}, Instruction[20]};  // Bit_Extender bit_extender_2
  Shifter #(.width(32)) shifter_2 (.in(bit_extender_2_out), .\dist (5'b01011), .out(shifter_2_out));
  assign bit_extender_3_out = {{22{1'b0}}, Instruction[30:21]};  // Bit_Extender bit_extender_3
  Shifter #(.width(32)) shifter_3 (.in(bit_extender_3_out), .\dist (5'b00001), .out(shifter_3_out));
  assign bit_extender_4_out = {{31{Instruction[31]}}, Instruction[31]};  // Bit_Extender bit_extender_4
  Shifter #(.width(32)) shifter_4 (.in(bit_extender_4_out), .\dist (5'b10100), .out(shifter_4_out));
  assign bit_extender_5_out = {{31{1'b0}}, Instruction[7]};  // Bit_Extender bit_extender_5
  assign bit_extender_6_out = {{28{1'b0}}, Instruction[11:8]};  // Bit_Extender bit_extender_6
  assign bit_extender_7_out = {{26{1'b0}}, Instruction[30:25]};  // Bit_Extender bit_extender_7
  assign bit_extender_8_out = {{31{Instruction[31]}}, Instruction[31]};  // Bit_Extender bit_extender_8
  Adder #(.width(32)) adder_1 (.a(shifter_1_out), .b(shifter_2_out), .out(adder_1_out));  // open: cin, cout
  Adder #(.width(32)) adder_2 (.a(shifter_3_out), .b(shifter_4_out), .out(adder_2_out));  // open: cin, cout
  Shifter #(.width(32)) shifter_5 (.in(bit_extender_5_out), .\dist (5'b01011), .out(shifter_5_out));
  Adder #(.width(32)) adder_3 (.a(shifter_5_out), .b(shifter_6_out), .out(adder_3_out));  // open: cin, cout
  Shifter #(.width(32)) shifter_6 (.in(bit_extender_6_out), .\dist (5'b00001), .out(shifter_6_out));
  Shifter #(.width(32)) shifter_7 (.in(bit_extender_7_out), .\dist (5'b00101), .out(shifter_7_out));
  Adder #(.width(32)) adder_4 (.a(shifter_7_out), .b(shifter_8_out), .out(adder_4_out));  // open: cin, cout
  Shifter #(.width(32)) shifter_8 (.in(bit_extender_8_out), .\dist (5'b01100), .out(shifter_8_out));
  Adder #(.width(32)) adder_5 (.a(adder_1_out), .b(adder_2_out), .out(ImmUJ));  // open: cin, cout
  Adder #(.width(32)) adder_6 (.a(adder_3_out), .b(adder_4_out), .out(ImmSB));  // open: cin, cout
  Multiplexer #(.select(5), .width(32), .disabled(0), .enable("false")) multiplexer_1 (
    .in0(ImmI), .in4(ImmI), .in8(ImmS), .in13(ImmU), .in24(ImmSB), .in25(ImmI), .in27(ImmUJ), .out(Imm),
    .sel(Opcode[6:2]));  // open: in1, in2, in3, in5, in6, in7, in9, in10, in11, in12, in14, in15, in16, in17, in18, in19, in20, in21, in22, in23, in26, in28, in29, in30, in31
  // Probe on Immediate
  Comparator #(.width(7)) comparator_1 (.a({7{1'b0}}), .b(funct7), .eq(comparator_1_eq));  // open: gt, lt
  Comparator #(.width(3)) comparator_2 (.a(3'b001), .b(funct3), .eq(comparator_2_eq));  // open: gt, lt
  Comparator #(.width(3)) comparator_3 (.a(3'b101), .b(funct3), .eq(comparator_3_eq));  // open: gt, lt
  Comparator #(.width(7), .mode("unsigned")) comparator_4 (
    .a(Opcode), .b(7'b0010011), .eq(comparator_4_eq));  // open: gt, lt
  assign bit_extender_9_out = {{12{Instruction[31]}}, Instruction[31:12]};  // Bit_Extender bit_extender_9
  assign ImmI = {{20{Instruction[31]}}, Instruction[31:20]};  // Bit_Extender bit_extender_10
  or or_1 (or_1_out, comparator_2_eq, comparator_3_eq);
  Shifter #(.width(32)) shifter_9 (.in(bit_extender_9_out), .\dist (5'b01100), .out(ImmU));
  assign bit_extender_11_out = {{27{1'b0}}, Instruction[11:7]};  // Bit_Extender bit_extender_11
  assign bit_extender_12_out = {{25{Instruction[31]}}, Instruction[31:25]};  // Bit_Extender bit_extender_12
  and and_1 (and_1_out, comparator_1_eq, or_1_out);
  Shifter #(.width(32)) shifter_10 (.in(bit_extender_12_out), .\dist (5'b00101), .out(shifter_10_out));
  Multiplexer #(.width(32), .disabled(0)) multiplexer_2 (
    .in0(Imm), .in1(bit_extender_13_out), .out(Immediate), .sel(and_2_out));  // open: en
  assign bit_extender_13_out = {{28{Imm[3]}}, Imm[3:0]};  // Bit_Extender bit_extender_13
  and and_2 (and_2_out, and_1_out, comparator_4_eq);
  Adder #(.width(32)) adder_7 (.a(bit_extender_11_out), .b(shifter_10_out), .out(ImmS));  // open: cin, cout

  // Other names for the same wires on the sheet: FinalImm[31:0] = Immediate; ImmSel[4:0] = Opcode[6:2]

  // Notes on the sheet:
  //   Sll
  //   Sll
endmodule

// AS
module ALUSel (
  input  [6:0] func7,
  input  [2:0] func3,
  input  PCSel,
  input  MemWEn,
  input  [6:0] OpCode,
  output [3:0] ALUSel
);

  wire and_1_out, and_2_out, and_3_out, and_4_out, and_5_out, and_6_out, and_7_out, and_8_out, and_9_out,
       and_10_out, and_11_out, and_12_out, and_13_out, and_14_out, and_15_out, and_16_out, comparator_1_eq,
       comparator_2_eq, comparator_3_eq, comparator_4_eq, comparator_5_eq, comparator_6_eq, comparator_7_eq,
       comparator_8_eq, comparator_9_eq, comparator_10_eq, comparator_11_eq, comparator_12_eq,
       comparator_13_eq, comparator_14_eq, comparator_15_eq, comparator_16_eq, comparator_17_eq,
       comparator_18_eq, comparator_19_eq, comparator_20_eq, comparator_21_eq, comparator_22_eq,
       comparator_23_eq, comparator_24_eq, comparator_25_eq, comparator_26_eq, comparator_27_eq,
       comparator_28_eq, comparator_29_eq, comparator_30_eq, comparator_31_eq, comparator_32_eq,
       comparator_33_eq, comparator_34_eq, comparator_35_eq, comparator_36_eq, comparator_37_eq,
       comparator_38_eq, comparator_39_eq, comparator_40_eq, comparator_41_eq, comparator_42_eq,
       comparator_43_eq, or_1_out, or_2_out, or_3_out, or_4_out, or_5_out, or_6_out, or_7_out;
  wire [3:0] step_1, step_2, step_3, step_4, step_5, step_6, step_7, step_8, step_9, step_10, step_11,
       step_12;

  Comparator #(.width(7), .mode("unsigned")) comparator_1 (
    .a(OpCode), .b(7'b0110011), .eq(comparator_1_eq));  // open: gt, lt
  Comparator #(.width(3)) comparator_2 (.a(3'b010), .b(func3), .eq(comparator_2_eq));  // open: gt, lt
  Comparator #(.width(7), .mode("unsigned")) comparator_3 (
    .a(OpCode), .b(7'b0110011), .eq(comparator_3_eq));  // open: gt, lt
  Comparator #(.width(7), .mode("unsigned")) comparator_4 (
    .a(OpCode), .b(7'b0010011), .eq(comparator_4_eq));  // open: gt, lt
  Comparator #(.width(3)) comparator_5 (.a(3'b001), .b(func3), .eq(comparator_5_eq));  // open: gt, lt
  Comparator #(.width(7)) comparator_6 (.a(7'b0000001), .b(func7), .eq(comparator_6_eq));  // open: gt, lt
  Comparator #(.width(3)) comparator_7 (.a(3'b000), .b(func3), .eq(comparator_7_eq));  // open: gt, lt
  Comparator #(.width(7), .mode("unsigned")) comparator_8 (
    .a(OpCode), .b(7'b0110011), .eq(comparator_8_eq));  // open: gt, lt
  Comparator #(.width(7)) comparator_9 (.a(7'b0000001), .b(func7), .eq(comparator_9_eq));  // open: gt, lt
  Comparator #(.width(3)) comparator_10 (.a(3'b000), .b(func3), .eq(comparator_10_eq));  // open: gt, lt
  Comparator #(.width(7)) comparator_11 (.a({7{1'b0}}), .b(func7), .eq(comparator_11_eq));  // open: gt, lt
  Comparator #(.width(7), .mode("unsigned")) comparator_12 (
    .a(OpCode), .b(7'b0010011), .eq(comparator_12_eq));  // open: gt, lt
  Comparator #(.width(3)) comparator_13 (.a(3'b000), .b(func3), .eq(comparator_13_eq));  // open: gt, lt
  Comparator #(.width(7), .mode("unsigned")) comparator_14 (
    .a(OpCode), .b(7'b0000011), .eq(comparator_14_eq));  // open: gt, lt
  Comparator #(.width(3)) comparator_15 (.a(3'b100), .b(func3), .eq(comparator_15_eq));  // open: gt, lt
  Comparator #(.width(7), .mode("unsigned")) comparator_16 (
    .a(OpCode), .b(7'b0010011), .eq(comparator_16_eq));  // open: gt, lt
  Comparator #(.width(3)) comparator_17 (.a(3'b100), .b(func3), .eq(comparator_17_eq));  // open: gt, lt
  Comparator #(.width(7)) comparator_18 (.a({7{1'b0}}), .b(func7), .eq(comparator_18_eq));  // open: gt, lt
  or or_1 (or_1_out, comparator_3_eq, comparator_4_eq);
  and and_1 (and_1_out, comparator_10_eq, comparator_11_eq);
  and and_2 (and_2_out, comparator_12_eq, comparator_13_eq);
  and and_3 (and_3_out, comparator_15_eq, comparator_16_eq);
  and and_4 (and_4_out, comparator_17_eq, comparator_1_eq, comparator_18_eq);
  Multiplexer #(.width(4), .disabled(0), .enable("false")) multiplexer_1 (
    .in0(step_4), .in1(4'b0110), .out(step_3), .sel(and_5_out));
  and and_5 (and_5_out, comparator_2_eq, or_1_out);
  Multiplexer #(.width(4), .disabled(0), .enable("false")) multiplexer_2 (
    .in0(step_3), .in1(4'b1000), .out(step_2), .sel(and_6_out));
  and and_6 (and_6_out, comparator_5_eq, comparator_6_eq);
  Multiplexer #(.width(4), .disabled(0)) multiplexer_3 (
    .in0(step_2), .in1(4'b0111), .out(step_1), .sel(and_7_out));  // open: en
  and and_7 (and_7_out, comparator_7_eq, comparator_8_eq, comparator_9_eq);
  or or_2 (or_2_out, and_1_out, and_2_out, MemWEn, PCSel, comparator_14_eq);
  or or_3 (or_3_out, and_3_out, and_4_out);
  Multiplexer #(.width(4), .disabled(0), .enable("false")) multiplexer_4 (
    .in0(step_1), .in1(4'b0010), .out(ALUSel), .sel(or_2_out));
  Multiplexer #(.width(4), .disabled(0), .enable("false")) multiplexer_5 (
    .in0(step_5), .in1(4'b0101), .out(step_4), .sel(or_3_out));
  Comparator #(.width(7), .mode("unsigned")) comparator_19 (
    .a(OpCode), .b(7'b0110011), .eq(comparator_19_eq));  // open: gt, lt
  Comparator #(.width(3)) comparator_20 (.a(3'b111), .b(func3), .eq(comparator_20_eq));  // open: gt, lt
  Comparator #(.width(7), .mode("unsigned")) comparator_21 (
    .a(OpCode), .b(7'b0110011), .eq(comparator_21_eq));  // open: gt, lt
  Comparator #(.width(7), .mode("unsigned")) comparator_22 (
    .a(OpCode), .b(7'b0010011), .eq(comparator_22_eq));  // open: gt, lt
  Comparator #(.width(7), .mode("unsigned")) comparator_23 (
    .a(OpCode), .b(7'b0110011), .eq(comparator_23_eq));  // open: gt, lt
  Comparator #(.width(7), .mode("unsigned")) comparator_24 (
    .a(OpCode), .b(7'b0110111), .eq(comparator_24_eq));  // open: gt, lt
  Comparator #(.width(7)) comparator_25 (.a({7{1'b0}}), .b(func7), .eq(comparator_25_eq));  // open: gt, lt
  Comparator #(.width(3)) comparator_26 (.a(3'b001), .b(func3), .eq(comparator_26_eq));  // open: gt, lt
  Comparator #(.width(7), .mode("unsigned")) comparator_27 (
    .a(OpCode), .b(7'b0110011), .eq(comparator_27_eq));  // open: gt, lt
  Comparator #(.width(7), .mode("unsigned")) comparator_28 (
    .a(OpCode), .b(7'b0010011), .eq(comparator_28_eq));  // open: gt, lt
  Comparator #(.width(7), .mode("unsigned")) comparator_29 (
    .a(OpCode), .b(7'b0110011), .eq(comparator_29_eq));  // open: gt, lt
  Comparator #(.width(7), .mode("unsigned")) comparator_30 (
    .a(OpCode), .b(7'b0110011), .eq(comparator_30_eq));  // open: gt, lt
  Comparator #(.width(7), .mode("unsigned")) comparator_31 (
    .a(OpCode), .b(7'b0010011), .eq(comparator_31_eq));  // open: gt, lt
  Comparator #(.width(3)) comparator_32 (.a(3'b110), .b(func3), .eq(comparator_32_eq));  // open: gt, lt
  Comparator #(.width(7), .mode("unsigned")) comparator_33 (
    .a(OpCode), .b(7'b0010011), .eq(comparator_33_eq));  // open: gt, lt
  Comparator #(.width(3)) comparator_34 (.a(3'b110), .b(func3), .eq(comparator_34_eq));  // open: gt, lt
  Comparator #(.width(7), .mode("unsigned")) comparator_35 (
    .a(OpCode), .b(7'b0110011), .eq(comparator_35_eq));  // open: gt, lt
  Comparator #(.width(7)) comparator_36 (.a({7{1'b0}}), .b(func7), .eq(comparator_36_eq));  // open: gt, lt
  Comparator #(.width(3)) comparator_37 (.a(3'b110), .b(func3), .eq(comparator_37_eq));  // open: gt, lt
  or or_4 (or_4_out, comparator_21_eq, comparator_22_eq);
  Comparator #(.width(3)) comparator_38 (.a(3'b000), .b(func3), .eq(comparator_38_eq));  // open: gt, lt
  Comparator #(.width(7)) comparator_39 (.a(7'b0100000), .b(func7), .eq(comparator_39_eq));  // open: gt, lt
  Multiplexer #(.width(4), .enable("false")) multiplexer_6 (
    .in0(step_12), .in1(4'b1100), .out(step_11), .sel(comparator_24_eq));
  or or_5 (or_5_out, comparator_27_eq, comparator_28_eq);
  Comparator #(.width(3)) comparator_40 (.a(3'b100), .b(func3), .eq(comparator_40_eq));  // open: gt, lt
  Comparator #(.width(7)) comparator_41 (.a(7'b0000001), .b(func7), .eq(comparator_41_eq));  // open: gt, lt
  or or_6 (or_6_out, comparator_30_eq, comparator_31_eq);
  Comparator #(.width(3)) comparator_42 (.a(3'b101), .b(func3), .eq(comparator_42_eq));  // open: gt, lt
  and and_8 (and_8_out, comparator_32_eq, comparator_33_eq);
  and and_9 (and_9_out, comparator_34_eq, comparator_35_eq, comparator_36_eq);
  Comparator #(.width(7)) comparator_43 (.a(7'b0000001), .b(func7), .eq(comparator_43_eq));  // open: gt, lt
  and and_10 (and_10_out, comparator_20_eq, or_4_out);
  and and_11 (and_11_out, comparator_38_eq, comparator_23_eq, comparator_39_eq);
  and and_12 (and_12_out, comparator_25_eq, comparator_26_eq);
  and and_13 (and_13_out, comparator_40_eq, comparator_29_eq, comparator_41_eq);
  and and_14 (and_14_out, or_6_out, comparator_42_eq);
  or or_7 (or_7_out, and_8_out, and_9_out);
  and and_15 (and_15_out, comparator_37_eq, comparator_19_eq, comparator_43_eq);
  Multiplexer #(.width(4), .disabled(0), .enable("false")) multiplexer_7 (
    .in0(step_10), .in1(4'b0011), .out(step_9), .sel(and_10_out));
  Multiplexer #(.width(4), .enable("false")) multiplexer_8 (
    .in0(step_11), .in1(4'b1011), .out(step_10), .sel(and_11_out));
  and and_16 (and_16_out, and_12_out, or_5_out);
  Multiplexer #(.width(4), .disabled(0), .enable("false")) multiplexer_9 (
    .in0(step_6), .in1(4'b1001), .out(step_5), .sel(and_13_out));
  Multiplexer #(.width(4), .disabled(0), .enable("false")) multiplexer_10 (
    .in0(step_7), .in1(4'b0001), .out(step_6), .sel(and_14_out));
  Multiplexer #(.width(4), .disabled(0), .enable("false")) multiplexer_11 (
    .in0(step_8), .in1(4'b0100), .out(step_7), .sel(or_7_out));
  Multiplexer #(.width(4), .disabled(0), .enable("false")) multiplexer_12 (
    .in0(step_9), .in1(4'b1010), .out(step_8), .sel(and_15_out));
  Multiplexer #(.width(4), .enable("false")) multiplexer_13 (
    .in1(4'b0000), .out(step_12), .sel(and_16_out));  // open: in0

  // Other names for the same wires on the sheet: val[3:0] = ALUSel

  // Notes on the sheet:
  //   Itype & func3= 0x4
  //   Xor
  //   Slt
  //   Mulh
  //   Mul
  //   Add
  //   Lui
  //   Sll
  //   div
  //   Rem
  //   And
  //   Sub
  //   Srl
  //   Or
endmodule

// BrCmp
module Branch_Comparator (
  input  [31:0] Instruction,
  input  [31:0] r1dat,
  input  [31:0] r2dat,
  output BrLT,
  output BrEq,
  output BrLTU
);

  wire comparator_1_eq, comparator_2_eq, comparator_3_eq, comparator_4_eq, comparator_5_eq, comparator_6_lt,
       comparator_7_eq, comparator_8_eq, comparator_9_lt;

  Comparator #(.width(7), .mode("unsigned")) comparator_1 (
    .a(Instruction[6:0]), .b(7'b1100011), .eq(comparator_1_eq));  // open: gt, lt
  Comparator #(.width(3), .mode("unsigned")) comparator_2 (
    .a(Instruction[14:12]), .b(3'b100), .eq(comparator_2_eq));  // open: gt, lt
  Comparator #(.width(32)) comparator_3 (.a(r1dat), .b(r2dat), .eq(comparator_3_eq));  // open: gt, lt
  Comparator #(.width(7), .mode("unsigned")) comparator_4 (
    .a(Instruction[6:0]), .b(7'b1100011), .eq(comparator_4_eq));  // open: gt, lt
  Comparator #(.width(3), .mode("unsigned")) comparator_5 (
    .a(Instruction[14:12]), .b(3'b000), .eq(comparator_5_eq));  // open: gt, lt
  Comparator #(.width(32), .mode("unsigned")) comparator_6 (
    .a(r1dat), .b(r2dat), .lt(comparator_6_lt));  // open: gt, eq
  Comparator #(.width(7), .mode("unsigned")) comparator_7 (
    .a(Instruction[6:0]), .b(7'b1100011), .eq(comparator_7_eq));  // open: gt, lt
  Comparator #(.width(3), .mode("unsigned")) comparator_8 (
    .a(Instruction[14:12]), .b(3'b110), .eq(comparator_8_eq));  // open: gt, lt
  Comparator #(.width(32)) comparator_9 (.a(r1dat), .b(r2dat), .lt(comparator_9_lt));  // open: gt, eq
  and and_1 (BrLT, comparator_9_lt, comparator_1_eq, comparator_2_eq);
  and and_2 (BrEq, comparator_3_eq, comparator_4_eq, comparator_5_eq);
  and and_3 (BrLTU, comparator_6_lt, comparator_7_eq, comparator_8_eq);

  // Other names for the same wires on the sheet: opcode[6:0] = Instruction[6:0]; rd[4:0] = Instruction[11:7];
  //   funct3[2:0] = Instruction[14:12]; rs1[4:0] = Instruction[19:15]; rs2[4:0] = Instruction[24:20];
  //   funct7[6:0] = Instruction[31:25]

  // Notes on the sheet:
  //   Branch Comparator
endmodule
