// Logisim project run.circ as structural Verilog: 1 circuit, main circuit main
module main (
  output [31:0] s0_Value,
  output [31:0] s1_Value,
  output [31:0] t0_Value,
  output [31:0] t1_Value,
  output [31:0] a0_Value,
  output [31:0] ra_Value,
  output [31:0] sp_Value,
  output [15:0] Time_Step,
  output [31:0] Requested_Address,
  output [31:0] Requested_Instruction
);

  wire clock_1_out;

  Clock clock_1 (.out(clock_1_out));
  cpu_main main_1 (
    .INSTRUCTION(Requested_Instruction), .CLOCK(clock_1_out), .FETCH_ADDRESS(Requested_Address),
    .s0_Value(s0_Value), .s1_Value(s1_Value), .t0_Value(t0_Value), .t1_Value(t1_Value), .sp_Value(sp_Value),
    .ra_Value(ra_Value), .a0_Value(a0_Value));
  Counter #(.width(16), .max('hffff)) counter_1 (.Q(Time_Step), .clk(clock_1_out));  // open: load, D, count, carry, clr
  // Probe on Requested_Address
  ROM #(.addrWidth(14), .dataWidth(32)) rom_1 (
    .addr(Requested_Address[13:0]), .data(Requested_Instruction));  // open: sel
  // Probe on Requested_Instruction

  // Other names for the same wires on the sheet: fetch_addr[31:0] = Requested_Address;
  //   Instruction[31:0] = Requested_Instruction

  // Notes on the sheet:
  //   YOUR CPU SHOULD FIT IN HERE!
  //   Instruction Memory
  //   contents of rom_1 (hex, n*v repeats v):
  //   300513 8000ef 54000ef 200293 4554463 ff410113 112023 a00433 812223 fff50513 fe5ff0ef 412403 a004b3
  //   912423 800533 ffe50513 fcdff0ef 812483 950533 12083 c10113 8067 8067
endmodule
